// Logisim project counter.circ as structural Verilog: 6 circuits, main circuit automat
// A
module main (
  input  [7:0] A,
  input  [7:0] B,
  output [7:0] A_2
);

  wire sn_1_tran_2, sn_2_tran_2, sn_3_tran_2, sn_4_tran_2, sn_5_tran_2, sn_6_tran_2, sn_7_tran_2;

  sn sn_1 (.A(A[0]), .B(B[0]), .Tran(1'b0), .Res(A_2[0]), .Tran_2(sn_1_tran_2));
  sn sn_2 (.A(A[1]), .B(B[1]), .Tran(sn_1_tran_2), .Res(A_2[1]), .Tran_2(sn_2_tran_2));
  sn sn_3 (.A(A[2]), .B(B[2]), .Tran(sn_2_tran_2), .Res(A_2[2]), .Tran_2(sn_3_tran_2));
  sn sn_4 (.A(A[3]), .B(B[3]), .Tran(sn_3_tran_2), .Res(A_2[3]), .Tran_2(sn_4_tran_2));
  sn sn_5 (.A(A[5]), .B(B[5]), .Tran(sn_6_tran_2), .Res(A_2[5]), .Tran_2(sn_5_tran_2));
  sn sn_6 (.A(A[4]), .B(B[4]), .Tran(sn_4_tran_2), .Res(A_2[4]), .Tran_2(sn_6_tran_2));
  sn sn_7 (.A(A[6]), .B(B[6]), .Tran(sn_5_tran_2), .Res(A_2[6]), .Tran_2(sn_7_tran_2));
  sn sn_8 (.A(A[7]), .B(B[7]), .Tran(sn_7_tran_2), .Res(A_2[7]));  // open: Tran_2
endmodule

module sn (
  input  A,
  input  B,
  input  Tran,
  output Res,
  output Tran_2
);

  wire and_1_out, and_2_out, xor_1_out;

  xor xor_1 (xor_1_out, A, B);
  xor xor_2 (Res, xor_1_out, Tran);
  and and_1 (and_1_out, xor_1_out, Tran);
  and and_2 (and_2_out, B, A);
  or or_1 (Tran_2, and_1_out, and_2_out);
endmodule

module generated (
  input  X1,
  input  X2,
  input  X3,
  input  X4,
  output Y1,
  output Y2,
  output Y3,
  output Y4
);

  wire and_1_out, and_2_out, and_3_out, and_4_out, and_5_out, and_6_out, and_7_out, and_8_out, and_9_out,
       and_10_out, not_1_out, not_2_out, not_3_out, not_4_out, not_5_out, not_6_out, not_7_out, not_8_out,
       not_9_out, not_10_out, not_11_out, not_12_out, not_13_out, not_14_out, not_15_out, not_16_out,
       not_17_out, not_18_out, not_19_out, not_20_out;

  not not_1 (not_1_out, X1);
  not not_2 (not_2_out, X3);
  not not_3 (not_3_out, X2);
  not not_4 (not_4_out, X2);
  not not_5 (not_5_out, X1);
  not not_6 (not_6_out, X1);
  not not_7 (not_7_out, X3);
  not not_8 (not_8_out, X4);
  not not_9 (not_9_out, X1);
  not not_10 (not_10_out, X3);
  not not_11 (not_11_out, X2);
  and and_1 (and_1_out, not_10_out, not_11_out, X4);
  not not_12 (not_12_out, X3);
  not not_13 (not_13_out, X1);
  and and_2 (and_2_out, not_12_out, not_13_out, X4);
  not not_14 (not_14_out, X4);
  and and_3 (and_3_out, X3, not_14_out, not_15_out);
  not not_15 (not_15_out, X1);
  not not_16 (not_16_out, X3);
  not not_17 (not_17_out, X2);
  and and_4 (and_4_out, not_16_out, not_17_out, not_18_out);
  not not_18 (not_18_out, X4);
  not not_19 (not_19_out, X4);
  and and_5 (and_5_out, not_19_out, not_20_out);
  not not_20 (not_20_out, X1);
  and and_6 (and_6_out, X2, X3, not_1_out, X4);
  or or_1 (Y1, and_6_out, and_7_out);
  and and_7 (and_7_out, not_2_out, not_3_out, X1);
  and and_8 (and_8_out, not_4_out, X3, not_5_out, X4);
  and and_9 (and_9_out, X2, not_6_out, not_7_out);
  or or_2 (Y2, and_8_out, and_9_out, and_10_out);
  and and_10 (and_10_out, X2, not_8_out, not_9_out);
  or or_3 (Y3, and_1_out, and_2_out, and_3_out);
  or or_4 (Y4, and_4_out, and_5_out);
endmodule

module d8421 (
  input  [3:0] in_1,
  output [3:0] out_2
);

  generated generated_1 (
    .X1(in_1[3]), .X2(in_1[2]), .X3(in_1[1]), .X4(in_1[0]), .Y1(out_2[3]), .Y2(out_2[2]), .Y3(out_2[1]),
    .Y4(out_2[0]));
endmodule

module automat (
  input  in_1
);

  wire clock_1_out, h_1_h1, h_1_h2, h_1_h3;
  wire [2:0] t_ff_3_q;

  Clock clock_1 (.out(clock_1_out));
  T_Flip_Flop t_ff_1 (.clk(clock_1_out), .T(h_1_h1), .Q(t_ff_3_q[2]));  // open: Qn, preset, reset
  T_Flip_Flop t_ff_2 (.clk(clock_1_out), .T(h_1_h2), .Q(t_ff_3_q[1]));  // open: Qn, preset, reset
  T_Flip_Flop t_ff_3 (.clk(clock_1_out), .T(h_1_h3), .Q(t_ff_3_q[0]));  // open: Qn, preset, reset
  H h_1 (.x1(t_ff_3_q[2]), .x2(t_ff_3_q[1]), .x3(t_ff_3_q[0]), .V(in_1), .h1(h_1_h1), .h2(h_1_h2), .h3(h_1_h3));
  Hex_Digit_Display hex_digit_display_1 (.value({1'b0, t_ff_3_q}));  // open: dp
endmodule

module H (
  input  x1,
  input  x2,
  input  x3,
  input  V,
  output h3,
  output h1,
  output h2
);

  wire nand_1_out, nand_3_out, or_1_out, or_2_out;

  nand nand_1 (nand_1_out, V, V);
  or or_1 (or_1_out, x2, x3, nand_1_out);
  nand nand_2 (h1, or_1_out, or_1_out);
  nand nand_3 (nand_3_out, V, V);
  or or_2 (or_2_out, x3, nand_3_out);
  nand nand_4 (h2, or_2_out, or_2_out);

  assign h3 = V;
endmodule
